# Fritzing sketch redes (saved by Fritzing 1.0.4)
breadboards: 1

parts:
  Mod1 = Heltec WiFi LoRa 32 V2 [part_number=HTIT-WB32LA]
  DHT1 = DHT11 Humitidy and Temperature Sensor (3 pins)
  Componente1 = Gas Sensor Breakout Board
  LED1 = smd LED [color="Red (633nm)" package="1206 [SMD]"]
  LED2 = smd LED [color="Green (570nm)" package="0805 [SMD]"]

nets:
  N1: Mod1.pin_5, LED1.anode
  N2: Mod1.pin_6, LED2.anode
  N3: Mod1.pin_11, Componente1.A2
  N4: Mod1.pin_16, Mod1.pin_17
  GND: Mod1.GND, DHT1.Gnd, Componente1.GND, LED1.cathode, LED2.cathode
  N5: Mod1.pin_20, DHT1.Plus, Componente1.B1
  N6: Mod1.pin_21, Mod1.pin_22
  N7: Mod1.pin_30, DHT1.Signal

custom parts:
  DHT11 Humitidy and Temperature Sensor (3 pins): DHT11 Humidity and Temperature Sensor (3 pins).
